// Logisim project Compute.circ as structural Verilog
module TickCounter (
  input  Clock,
  input  Enable,
  output out_3,
  output out_4,
  output out_5,
  output out_6
);

  wire not_1_out, O1, O2;

  T_Flip_Flop t_ff_1 (.clk(Clock), .T(1'b1), .Q(O1), .reset(not_1_out), .en(Enable));  // open: Qn, preset
  T_Flip_Flop t_ff_2 (.clk(O1), .T(1'b1), .Q(O2), .reset(not_1_out), .en(Enable));  // open: Qn, preset
  not not_1 (not_1_out, Enable);
  Demultiplexer #(.select(2), .disabled(0), .enable("false")) demultiplexer_1 (
    .out0(out_3), .out1(out_4), .out2(out_5), .out3(out_6), .in(Enable), .sel({O2, O1}));

  // Other names for the same wires on the sheet: CK = Clock; EN = Enable
endmodule

module _8BitIncrement (
  input  Clock,
  input  Enable,
  input  [7:0] Set,
  output [7:0] out_4
);

  wire not_1_out, not_2_out, not_3_out, not_4_out, not_5_out, not_7_out, not_8_out, not_9_out, O1, O2, O3,
       O4, O5, O6, O7, O8;
  wire [7:0] controlled_inverter_1_out;

  assign controlled_inverter_1_out = Clock ? ~Set : 8'bz;  // Controlled_Inverter controlled_inverter_1
  T_Flip_Flop t_ff_1 (
    .clk(Clock), .T(1'b1), .Q(O1), .preset(controlled_inverter_1_out[0]), .reset(not_1_out), .en(Enable));  // open: Qn
  not not_1 (not_1_out, controlled_inverter_1_out[0]);
  T_Flip_Flop t_ff_2 (
    .clk(O1), .T(1'b1), .Q(O2), .preset(controlled_inverter_1_out[1]), .reset(not_2_out), .en(Enable));  // open: Qn
  not not_2 (not_2_out, controlled_inverter_1_out[1]);
  T_Flip_Flop t_ff_3 (
    .clk(O2), .T(1'b1), .Q(O3), .preset(controlled_inverter_1_out[2]), .reset(not_3_out), .en(Enable));  // open: Qn
  not not_3 (not_3_out, controlled_inverter_1_out[2]);
  T_Flip_Flop t_ff_4 (
    .clk(O3), .T(1'b1), .Q(O4), .preset(controlled_inverter_1_out[3]), .reset(not_4_out), .en(Enable));  // open: Qn
  not not_4 (not_4_out, controlled_inverter_1_out[3]);
  T_Flip_Flop t_ff_5 (
    .clk(O4), .T(1'b1), .Q(O5), .preset(controlled_inverter_1_out[4]), .reset(not_5_out), .en(Enable));  // open: Qn
  not not_5 (not_5_out, controlled_inverter_1_out[4]);
  // NOT_Gate not_6 is placed but not wired
  T_Flip_Flop t_ff_6 (
    .clk(O5), .T(1'b1), .Q(O6), .preset(controlled_inverter_1_out[5]), .reset(not_7_out), .en(Enable));  // open: Qn
  not not_7 (not_7_out, controlled_inverter_1_out[5]);
  T_Flip_Flop t_ff_7 (
    .clk(O6), .T(1'b1), .Q(O7), .preset(controlled_inverter_1_out[6]), .reset(not_8_out), .en(Enable));  // open: Qn
  not not_8 (not_8_out, controlled_inverter_1_out[6]);
  T_Flip_Flop t_ff_8 (
    .clk(O7), .T(1'b1), .Q(O8), .preset(controlled_inverter_1_out[7]), .reset(not_9_out), .en(Enable));  // open: Qn
  not not_9 (not_9_out, controlled_inverter_1_out[7]);
  assign out_4 = ~{O8, O7, O6, O5, O4, O3, O2, O1};  // NOT_Gate not_10, 8 bits wide

  // Other names for the same wires on the sheet: CK = Clock; EN = Enable; ST[7:0] = Set
endmodule

module CommandController (
  input  Clock,
  input  Enable,
  input  [7:0] Set_IC,
  output [4:0] Adress,
  output [2:0] OP_Code
);

  wire [7:0] controlled_buffer_1_out, n8bitincrement_1_out_4, rom_1_data;

  _8BitIncrement u_8bitincrement_1 (.Clock(Clock), .Enable(Enable), .out_4(n8bitincrement_1_out_4), .Set(Set_IC));
  assign controlled_buffer_1_out = Enable ? rom_1_data : 8'bz;  // Controlled_Buffer controlled_buffer_1
  ROM rom_1 (.addr(n8bitincrement_1_out_4), .data(rom_1_data), .sel(Enable));
  Register #(.width(5)) register_1 (
    .D(controlled_buffer_1_out[4:0]), .en(Enable), .Q(Adress), .clk(Clock));  // open: clr
  Register #(.width(3)) register_2 (
    .D(controlled_buffer_1_out[7:5]), .en(Enable), .Q(OP_Code), .clk(Clock));  // open: clr

  // Other names for the same wires on the sheet: CLK = Clock; ENB = Enable; SIC[7:0] = Set_IC

  // Notes on the sheet:
  //   contents of rom_1 (hex, n*v repeats v):
  //   aa 0 aa 29*0 11
endmodule

module Computer (
  input  RN
);

  wire CK, T0, T1, T2, T3;

  Clock clock_1 (.out(CK));
  TickCounter tickcounter_1 (.Clock(CK), .Enable(RN), .out_6(T1), .out_5(T0), .out_4(T2), .out_3(T3));
  CommandController commandcontroller_1 ();  // open: Clock, Set_IC, Enable, Adress, OP_Code
endmodule
